// Logisim project processador.circ as structural Verilog: 19 circuits, main circuit main
module main (
);

  wire ALUSrc, and_1_out, Branch, clock_1_out, EDisplay, Jump, MemToReg, ula_1_zero, WriteReg;
  wire [2:0] ALUOp;
  wire [3:0] Opcode, RA, RB, RC;
  wire [15:0] Const;
  wire [31:0] bancoderegistradores_1_readdataa, bancoderegistradores_1_readdatab, extensorsinal_1_b,
       extensorzero_1_b, multiplexer_1_out, multiplexer_2_out, multiplexer_3_out, multiplexer_4_out,
       multiplexer_5_out, registrador_32bits_pc_1_q, somador_32bits_1_s, somador_32bits_2_s, ula_1_s;

  Clock clock_1 (.out(clock_1_out));
  Multiplexer #(.width(32)) multiplexer_1 (
    .in0(multiplexer_2_out), .in1(extensorsinal_1_b), .out(multiplexer_1_out), .sel(Jump));
  Multiplexer #(.width(32)) multiplexer_2 (
    .in0(somador_32bits_1_s), .in1(somador_32bits_2_s), .out(multiplexer_2_out), .sel(and_1_out));
  and and_1 (and_1_out, Branch, ula_1_zero);
  Somador_32bits somador_32bits_1 (.Ci(1'b0), .A(registrador_32bits_pc_1_q), .B(32'h1), .S(somador_32bits_1_s));
  Somador_32bits somador_32bits_2 (
    .Ci(1'b0), .A(registrador_32bits_pc_1_q), .B(extensorsinal_1_b), .S(somador_32bits_2_s));
  ExtensorSinal extensorsinal_1 (.A(Const), .B(extensorsinal_1_b));
  Registrador_32bits_PC registrador_32bits_pc_1 (
    .D(multiplexer_1_out), .Clk(clock_1_out), .Q(registrador_32bits_pc_1_q));
  ROM #(.addrWidth(14), .dataWidth(32)) MemoriaInstrucao (
    .addr(registrador_32bits_pc_1_q[13:0]), .data({Opcode, RA, RB, RC, Const}));
  ROM #(.addrWidth(4), .dataWidth(9)) MemoriaControle (
    .addr(Opcode), .data({ALUSrc, ALUOp, WriteReg, EDisplay, Branch, MemToReg, Jump}));
  BancoDeRegistradores bancoderegistradores_1 (
    .Clk(clock_1_out), .Dado(multiplexer_5_out), .readRegA(RA), .WriteReg(WriteReg), .C(RC), .ReadRegB(RB),
    .readDataA(bancoderegistradores_1_readdataa), .readDataB(bancoderegistradores_1_readdatab));
  ExtensorZero extensorzero_1 (.A(Const), .B(extensorzero_1_b));
  Multiplexer #(.width(32)) multiplexer_3 (
    .in0({32{1'b0}}), .in1(bancoderegistradores_1_readdataa), .out(multiplexer_3_out), .sel(EDisplay));
  Multiplexer #(.width(32)) multiplexer_4 (
    .in0(bancoderegistradores_1_readdatab), .in1(extensorzero_1_b), .out(multiplexer_4_out), .sel(ALUSrc));
  // Probe on multiplexer_3_out
  ULA ula_1 (
    .Funct(ALUOp), .A(bancoderegistradores_1_readdataa), .B(multiplexer_4_out), .Zero(ula_1_zero), .S(ula_1_s));
  Multiplexer #(.width(32)) multiplexer_5 (
    .in0(ula_1_s), .in1(extensorzero_1_b), .out(multiplexer_5_out), .sel(MemToReg));

  // Notes on the sheet:
  //   contents of MemoriaInstrucao (hex, n*v repeats v):
  //   0 10010003 10020007 10030012 10040000 10050000 c5100007 45360000 26260000 24640000 d4000000 95050001
  //   b0000006 d4000000 e000fff3
  //   contents of MemoriaControle (hex, n*v repeats v):
  //   0 112 10 30 50 70 90 b0 d0 110 130 105 24 8 e0
endmodule

module Registrador_4bits (
  input  D0,
  input  D1,
  input  D2,
  input  D3,
  input  E,
  input  Clk,
  output Q0,
  output Q1,
  output Q2,
  output Q3
);

  wire d_ff_1_qn, d_ff_2_qn, d_ff_3_qn, d_ff_4_qn, multiplexer_1_out, multiplexer_2_out, multiplexer_3_out,
       multiplexer_4_out;

  Multiplexer multiplexer_1 (.in0(Q0), .in1(D0), .out(multiplexer_1_out), .sel(E));
  Multiplexer multiplexer_2 (.in0(Q1), .in1(D1), .out(multiplexer_2_out), .sel(E));
  Multiplexer multiplexer_3 (.in0(Q2), .in1(D2), .out(multiplexer_3_out), .sel(E));
  Multiplexer multiplexer_4 (.in0(Q3), .in1(D3), .out(multiplexer_4_out), .sel(E));
  D_Flip_Flop d_ff_1 (.D(multiplexer_1_out), .clk(Clk), .Q(Q0), .Qn(d_ff_1_qn));  // open: preset, reset
  D_Flip_Flop d_ff_2 (.D(multiplexer_2_out), .clk(Clk), .Q(Q1), .Qn(d_ff_2_qn));  // open: preset, reset
  D_Flip_Flop d_ff_3 (.D(multiplexer_3_out), .clk(Clk), .Q(Q2), .Qn(d_ff_3_qn));  // open: preset, reset
  D_Flip_Flop d_ff_4 (.D(multiplexer_4_out), .clk(Clk), .Q(Q3), .Qn(d_ff_4_qn));  // open: preset, reset
endmodule

module Registrador_32bits (
  input  E,
  input  [31:0] D,
  input  Clk,
  output [31:0] Q
);

  Registrador_4bits registrador_4bits_1 (
    .D0(D[0]), .D1(D[1]), .D2(D[2]), .D3(D[3]), .E(E), .Clk(Clk), .Q0(Q[0]), .Q1(Q[1]), .Q2(Q[2]), .Q3(Q[3]));
  Registrador_4bits registrador_4bits_2 (
    .D0(D[4]), .D1(D[5]), .D2(D[6]), .D3(D[7]), .E(E), .Clk(Clk), .Q0(Q[4]), .Q1(Q[5]), .Q2(Q[6]), .Q3(Q[7]));
  Registrador_4bits registrador_4bits_3 (
    .D0(D[8]), .D1(D[9]), .D2(D[10]), .D3(D[11]), .E(E), .Clk(Clk), .Q0(Q[8]), .Q1(Q[9]), .Q2(Q[10]),
    .Q3(Q[11]));
  Registrador_4bits registrador_4bits_4 (
    .D0(D[12]), .D1(D[13]), .D2(D[14]), .D3(D[15]), .E(E), .Clk(Clk), .Q0(Q[12]), .Q1(Q[13]), .Q2(Q[14]),
    .Q3(Q[15]));
  Registrador_4bits registrador_4bits_5 (
    .D0(D[16]), .D1(D[17]), .D2(D[18]), .D3(D[19]), .E(E), .Clk(Clk), .Q0(Q[16]), .Q1(Q[17]), .Q2(Q[18]),
    .Q3(Q[19]));
  Registrador_4bits registrador_4bits_6 (
    .D0(D[20]), .D1(D[21]), .D2(D[22]), .D3(D[23]), .E(E), .Clk(Clk), .Q0(Q[20]), .Q1(Q[21]), .Q2(Q[22]),
    .Q3(Q[23]));
  Registrador_4bits registrador_4bits_7 (
    .D0(D[24]), .D1(D[25]), .D2(D[26]), .D3(D[27]), .E(E), .Clk(Clk), .Q0(Q[24]), .Q1(Q[25]), .Q2(Q[26]),
    .Q3(Q[27]));
  Registrador_4bits registrador_4bits_8 (
    .D0(D[28]), .D1(D[29]), .D2(D[30]), .D3(D[31]), .E(E), .Clk(Clk), .Q0(Q[28]), .Q1(Q[29]), .Q2(Q[30]),
    .Q3(Q[31]));
endmodule

module BancoDeRegistradoresV1 (
  input  Clk,
  input  [31:0] write_data,
  input  [3:0] readRegA,
  input  [3:0] RegLeitura4,
  input  [3:0] RegLeitura8,
  input  [3:0] RegLeitura12,
  input  reg_write,
  input  [3:0] write_registers,
  input  [3:0] RegLeitura1,
  input  [3:0] RegLeitura5,
  input  [3:0] RegLeitura9,
  input  [3:0] RegLeitura13,
  input  [3:0] RegLeitura2,
  input  [3:0] RegLeitura6,
  input  [3:0] RegLeitura10,
  input  [3:0] RegLeitura14,
  input  [3:0] RegLeitura3,
  input  [3:0] RegLeitura7,
  input  [3:0] RegLeitura11,
  input  [3:0] RegLeitura15,
  output [31:0] A,
  output [31:0] R4,
  output [31:0] R8,
  output [31:0] R12,
  output [31:0] R1,
  output [31:0] R5,
  output [31:0] R9,
  output [31:0] R13,
  output [31:0] R2,
  output [31:0] R6,
  output [31:0] R10,
  output [31:0] R14,
  output [31:0] R3,
  output [31:0] R7,
  output [31:0] R11,
  output [31:0] R15
);

  wire and_1_out, demultiplexer_1_out0, demultiplexer_1_out1, demultiplexer_1_out2, demultiplexer_1_out3,
       demultiplexer_1_out4, demultiplexer_1_out5, demultiplexer_1_out6, demultiplexer_1_out7,
       demultiplexer_1_out8, demultiplexer_1_out9, demultiplexer_1_out10, demultiplexer_1_out11,
       demultiplexer_1_out12, demultiplexer_1_out13, demultiplexer_1_out14, demultiplexer_1_out15;
  wire [31:0] Q0, Q1, Q2, Q3, Q4, Q5, Q6, Q7, Q8, Q9, Q10, Q11, Q12, Q13, Q14, Q15;

  Demultiplexer #(.select(4)) demultiplexer_1 (
    .out0(demultiplexer_1_out0), .out1(demultiplexer_1_out1), .out2(demultiplexer_1_out2),
    .out3(demultiplexer_1_out3), .out4(demultiplexer_1_out4), .out5(demultiplexer_1_out5),
    .out6(demultiplexer_1_out6), .out7(demultiplexer_1_out7), .out8(demultiplexer_1_out8),
    .out9(demultiplexer_1_out9), .out10(demultiplexer_1_out10), .out11(demultiplexer_1_out11),
    .out12(demultiplexer_1_out12), .out13(demultiplexer_1_out13), .out14(demultiplexer_1_out14),
    .out15(demultiplexer_1_out15), .in(reg_write), .sel(write_registers));
  and and_1 (and_1_out, 1'b0, demultiplexer_1_out0);
  Registrador_32bits registrador_32bits_1 (.E(and_1_out), .D(write_data), .Clk(Clk), .Q(Q0));
  Registrador_32bits registrador_32bits_2 (.E(demultiplexer_1_out1), .D(write_data), .Clk(Clk), .Q(Q1));
  Registrador_32bits registrador_32bits_3 (.E(demultiplexer_1_out2), .D(write_data), .Clk(Clk), .Q(Q2));
  Registrador_32bits registrador_32bits_4 (.E(demultiplexer_1_out3), .D(write_data), .Clk(Clk), .Q(Q3));
  Registrador_32bits registrador_32bits_5 (.E(demultiplexer_1_out8), .D(write_data), .Clk(Clk), .Q(Q8));
  Registrador_32bits registrador_32bits_6 (.E(demultiplexer_1_out9), .D(write_data), .Clk(Clk), .Q(Q9));
  Registrador_32bits registrador_32bits_7 (.E(demultiplexer_1_out10), .D(write_data), .Clk(Clk), .Q(Q10));
  Registrador_32bits registrador_32bits_8 (.E(demultiplexer_1_out11), .D(write_data), .Clk(Clk), .Q(Q11));
  Registrador_32bits registrador_32bits_9 (.E(demultiplexer_1_out4), .D(write_data), .Clk(Clk), .Q(Q4));
  Registrador_32bits registrador_32bits_10 (.E(demultiplexer_1_out5), .D(write_data), .Clk(Clk), .Q(Q5));
  Registrador_32bits registrador_32bits_11 (.E(demultiplexer_1_out6), .D(write_data), .Clk(Clk), .Q(Q6));
  Registrador_32bits registrador_32bits_12 (.E(demultiplexer_1_out7), .D(write_data), .Clk(Clk), .Q(Q7));
  Registrador_32bits registrador_32bits_13 (.E(demultiplexer_1_out12), .D(write_data), .Clk(Clk), .Q(Q12));
  Registrador_32bits registrador_32bits_14 (.E(demultiplexer_1_out13), .D(write_data), .Clk(Clk), .Q(Q13));
  Registrador_32bits registrador_32bits_15 (.E(demultiplexer_1_out14), .D(write_data), .Clk(Clk), .Q(Q14));
  Registrador_32bits registrador_32bits_16 (.E(demultiplexer_1_out15), .D(write_data), .Clk(Clk), .Q(Q15));
  Multiplexer #(.select(4), .width(32)) multiplexer_1 (
    .in0(Q0), .in1(Q1), .in2(Q2), .in3(Q3), .in4(Q4), .in5(Q5), .in6(Q6), .in7(Q7), .in8(Q8), .in9(Q9),
    .in10(Q10), .in11(Q11), .in12(Q12), .in13(Q13), .in14(Q14), .in15(Q15), .out(A), .sel(readRegA));
  Multiplexer #(.select(4), .width(32)) multiplexer_2 (
    .in0(Q0), .in1(Q1), .in2(Q2), .in3(Q3), .in4(Q4), .in5(Q5), .in6(Q6), .in7(Q7), .in8(Q8), .in9(Q9),
    .in10(Q10), .in11(Q11), .in12(Q12), .in13(Q13), .in14(Q14), .in15(Q15), .out(R1), .sel(RegLeitura1));
  Multiplexer #(.select(4), .width(32)) multiplexer_3 (
    .in0(Q0), .in1(Q1), .in2(Q2), .in3(Q3), .in4(Q4), .in5(Q5), .in6(Q6), .in7(Q7), .in8(Q8), .in9(Q9),
    .in10(Q10), .in11(Q11), .in12(Q12), .in13(Q13), .in14(Q14), .in15(Q15), .out(R2), .sel(RegLeitura2));
  Multiplexer #(.select(4), .width(32)) multiplexer_4 (
    .in0(Q0), .in1(Q1), .in2(Q2), .in3(Q3), .in4(Q4), .in5(Q5), .in6(Q6), .in7(Q7), .in8(Q8), .in9(Q9),
    .in10(Q10), .in11(Q11), .in12(Q12), .in13(Q13), .in14(Q14), .in15(Q15), .out(R3), .sel(RegLeitura3));
  Multiplexer #(.select(4), .width(32)) multiplexer_5 (
    .in0(Q0), .in1(Q1), .in2(Q2), .in3(Q3), .in4(Q4), .in5(Q5), .in6(Q6), .in7(Q7), .in8(Q8), .in9(Q9),
    .in10(Q10), .in11(Q11), .in12(Q12), .in13(Q13), .in14(Q14), .in15(Q15), .out(R4), .sel(RegLeitura4));
  Multiplexer #(.select(4), .width(32)) multiplexer_6 (
    .in0(Q0), .in1(Q1), .in2(Q2), .in3(Q3), .in4(Q4), .in5(Q5), .in6(Q6), .in7(Q7), .in8(Q8), .in9(Q9),
    .in10(Q10), .in11(Q11), .in12(Q12), .in13(Q13), .in14(Q14), .in15(Q15), .out(R5), .sel(RegLeitura5));
  Multiplexer #(.select(4), .width(32)) multiplexer_7 (
    .in0(Q0), .in1(Q1), .in2(Q2), .in3(Q3), .in4(Q4), .in5(Q5), .in6(Q6), .in7(Q7), .in8(Q8), .in9(Q9),
    .in10(Q10), .in11(Q11), .in12(Q12), .in13(Q13), .in14(Q14), .in15(Q15), .out(R6), .sel(RegLeitura6));
  Multiplexer #(.select(4), .width(32)) multiplexer_8 (
    .in0(Q0), .in1(Q1), .in2(Q2), .in3(Q3), .in4(Q4), .in5(Q5), .in6(Q6), .in7(Q7), .in8(Q8), .in9(Q9),
    .in10(Q10), .in11(Q11), .in12(Q12), .in13(Q13), .in14(Q14), .in15(Q15), .out(R7), .sel(RegLeitura7));
  Multiplexer #(.select(4), .width(32)) multiplexer_9 (
    .in0(Q0), .in1(Q1), .in2(Q2), .in3(Q3), .in4(Q4), .in5(Q5), .in6(Q6), .in7(Q7), .in8(Q8), .in9(Q9),
    .in10(Q10), .in11(Q11), .in12(Q12), .in13(Q13), .in14(Q14), .in15(Q15), .out(R8), .sel(RegLeitura8));
  Multiplexer #(.select(4), .width(32)) multiplexer_10 (
    .in0(Q0), .in1(Q1), .in2(Q2), .in3(Q3), .in4(Q4), .in5(Q5), .in6(Q6), .in7(Q7), .in8(Q8), .in9(Q9),
    .in10(Q10), .in11(Q11), .in12(Q12), .in13(Q13), .in14(Q14), .in15(Q15), .out(R9), .sel(RegLeitura9));
  Multiplexer #(.select(4), .width(32)) multiplexer_11 (
    .in0(Q0), .in1(Q1), .in2(Q2), .in3(Q3), .in4(Q4), .in5(Q5), .in6(Q6), .in7(Q7), .in8(Q8), .in9(Q9),
    .in10(Q10), .in11(Q11), .in12(Q12), .in13(Q13), .in14(Q14), .in15(Q15), .out(R10), .sel(RegLeitura10));
  Multiplexer #(.select(4), .width(32)) multiplexer_12 (
    .in0(Q0), .in1(Q1), .in2(Q2), .in3(Q3), .in4(Q4), .in5(Q5), .in6(Q6), .in7(Q7), .in8(Q8), .in9(Q9),
    .in10(Q10), .in11(Q11), .in12(Q12), .in13(Q13), .in14(Q14), .in15(Q15), .out(R11), .sel(RegLeitura11));
  Multiplexer #(.select(4), .width(32)) multiplexer_13 (
    .in0(Q0), .in1(Q1), .in2(Q2), .in3(Q3), .in4(Q4), .in5(Q5), .in6(Q6), .in7(Q7), .in8(Q8), .in9(Q9),
    .in10(Q10), .in11(Q11), .in12(Q12), .in13(Q13), .in14(Q14), .in15(Q15), .out(R12), .sel(RegLeitura12));
  Multiplexer #(.select(4), .width(32)) multiplexer_14 (
    .in0(Q0), .in1(Q1), .in2(Q2), .in3(Q3), .in4(Q4), .in5(Q5), .in6(Q6), .in7(Q7), .in8(Q8), .in9(Q9),
    .in10(Q10), .in11(Q11), .in12(Q12), .in13(Q13), .in14(Q14), .in15(Q15), .out(R13), .sel(RegLeitura13));
  Multiplexer #(.select(4), .width(32)) multiplexer_15 (
    .in0(Q0), .in1(Q1), .in2(Q2), .in3(Q3), .in4(Q4), .in5(Q5), .in6(Q6), .in7(Q7), .in8(Q8), .in9(Q9),
    .in10(Q10), .in11(Q11), .in12(Q12), .in13(Q13), .in14(Q14), .in15(Q15), .out(R14), .sel(RegLeitura14));
  Multiplexer #(.select(4), .width(32)) multiplexer_16 (
    .in0(Q0), .in1(Q1), .in2(Q2), .in3(Q3), .in4(Q4), .in5(Q5), .in6(Q6), .in7(Q7), .in8(Q8), .in9(Q9),
    .in10(Q10), .in11(Q11), .in12(Q12), .in13(Q13), .in14(Q14), .in15(Q15), .out(R15), .sel(RegLeitura15));

  // Notes on the sheet:
  //   RegLeitura2: initial=0x2
  //   RegLeitura1: initial=0x1
  //   Reg0
endmodule

module BancoDeRegistradores (
  input  Clk,
  input  [31:0] Dado,
  input  [3:0] readRegA,
  input  WriteReg,
  input  [3:0] C,
  input  [3:0] ReadRegB,
  output [31:0] readDataA,
  output [31:0] readDataB
);

  wire and_1_out, demultiplexer_1_out0, demultiplexer_1_out1, demultiplexer_1_out2, demultiplexer_1_out3,
       demultiplexer_1_out4, demultiplexer_1_out5, demultiplexer_1_out6, demultiplexer_1_out7,
       demultiplexer_1_out8, demultiplexer_1_out9, demultiplexer_1_out10, demultiplexer_1_out11,
       demultiplexer_1_out12, demultiplexer_1_out13, demultiplexer_1_out14, demultiplexer_1_out15;
  wire [31:0] Q0, Q1, Q2, Q3, Q4, Q5, Q6, Q7, Q8, Q9, Q10, Q11, Q12, Q13, Q14, Q15;

  Demultiplexer #(.select(4)) demultiplexer_1 (
    .out0(demultiplexer_1_out0), .out1(demultiplexer_1_out1), .out2(demultiplexer_1_out2),
    .out3(demultiplexer_1_out3), .out4(demultiplexer_1_out4), .out5(demultiplexer_1_out5),
    .out6(demultiplexer_1_out6), .out7(demultiplexer_1_out7), .out8(demultiplexer_1_out8),
    .out9(demultiplexer_1_out9), .out10(demultiplexer_1_out10), .out11(demultiplexer_1_out11),
    .out12(demultiplexer_1_out12), .out13(demultiplexer_1_out13), .out14(demultiplexer_1_out14),
    .out15(demultiplexer_1_out15), .in(WriteReg), .sel(C));
  and and_1 (and_1_out, 1'b0, demultiplexer_1_out0);
  Registrador_32bits registrador_32bits_1 (.E(and_1_out), .D(Dado), .Clk(Clk), .Q(Q0));
  Registrador_32bits registrador_32bits_2 (.E(demultiplexer_1_out1), .D(Dado), .Clk(Clk), .Q(Q1));
  Registrador_32bits registrador_32bits_3 (.E(demultiplexer_1_out2), .D(Dado), .Clk(Clk), .Q(Q2));
  Registrador_32bits registrador_32bits_4 (.E(demultiplexer_1_out3), .D(Dado), .Clk(Clk), .Q(Q3));
  Registrador_32bits registrador_32bits_5 (.E(demultiplexer_1_out8), .D(Dado), .Clk(Clk), .Q(Q8));
  Registrador_32bits registrador_32bits_6 (.E(demultiplexer_1_out9), .D(Dado), .Clk(Clk), .Q(Q9));
  Registrador_32bits registrador_32bits_7 (.E(demultiplexer_1_out10), .D(Dado), .Clk(Clk), .Q(Q10));
  Registrador_32bits registrador_32bits_8 (.E(demultiplexer_1_out11), .D(Dado), .Clk(Clk), .Q(Q11));
  Registrador_32bits registrador_32bits_9 (.E(demultiplexer_1_out4), .D(Dado), .Clk(Clk), .Q(Q4));
  Registrador_32bits registrador_32bits_10 (.E(demultiplexer_1_out5), .D(Dado), .Clk(Clk), .Q(Q5));
  Registrador_32bits registrador_32bits_11 (.E(demultiplexer_1_out6), .D(Dado), .Clk(Clk), .Q(Q6));
  Registrador_32bits registrador_32bits_12 (.E(demultiplexer_1_out7), .D(Dado), .Clk(Clk), .Q(Q7));
  Registrador_32bits registrador_32bits_13 (.E(demultiplexer_1_out12), .D(Dado), .Clk(Clk), .Q(Q12));
  Registrador_32bits registrador_32bits_14 (.E(demultiplexer_1_out13), .D(Dado), .Clk(Clk), .Q(Q13));
  Registrador_32bits registrador_32bits_15 (.E(demultiplexer_1_out14), .D(Dado), .Clk(Clk), .Q(Q14));
  Registrador_32bits registrador_32bits_16 (.E(demultiplexer_1_out15), .D(Dado), .Clk(Clk), .Q(Q15));
  Multiplexer #(.select(4), .width(32)) multiplexer_1 (
    .in0(Q0), .in1(Q1), .in2(Q2), .in3(Q3), .in4(Q4), .in5(Q5), .in6(Q6), .in7(Q7), .in8(Q8), .in9(Q9),
    .in10(Q10), .in11(Q11), .in12(Q12), .in13(Q13), .in14(Q14), .in15(Q15), .out(readDataA), .sel(readRegA));
  Multiplexer #(.select(4), .width(32)) multiplexer_2 (
    .in0(Q0), .in1(Q1), .in2(Q2), .in3(Q3), .in4(Q4), .in5(Q5), .in6(Q6), .in7(Q7), .in8(Q8), .in9(Q9),
    .in10(Q10), .in11(Q11), .in12(Q12), .in13(Q13), .in14(Q14), .in15(Q15), .out(readDataB), .sel(ReadRegB));

  // Notes on the sheet:
  //   ReadRegB: initial=0x1
  //   Reg0
endmodule

module AND_32bits (
  input  [31:0] A,
  input  [31:0] B,
  output [31:0] Y
);

  assign Y = A & B;  // AND_Gate and_1, 32 bits wide
endmodule

module OR_32bits (
  input  [31:0] A,
  input  [31:0] B,
  output [31:0] Y
);

  assign Y = A | B;  // OR_Gate or_1, 32 bits wide
endmodule

module XOR_32bits (
  input  [31:0] A,
  input  [31:0] B,
  output [31:0] Y
);

  assign Y = A ^ B;  // XOR_Gate xor_1, 32 bits wide
endmodule

module Multiplicador_32bits (
  input  [31:0] A,
  input  [31:0] B,
  output [31:0] Y
);

  Multiplier #(.width(32)) multiplier_1 (.a(A), .b(B), .out(Y));  // open: cin, cout
endmodule

module Somador_32bits (
  input  Ci,
  input  [31:0] A,
  input  [31:0] B,
  output [31:0] S
);

  wire somador_1bit_1_co, somador_1bit_2_co, somador_1bit_3_co, somador_1bit_4_co, somador_1bit_5_co,
       somador_1bit_6_co, somador_1bit_7_co, somador_1bit_8_co, somador_1bit_9_co, somador_1bit_10_co,
       somador_1bit_11_co, somador_1bit_12_co, somador_1bit_13_co, somador_1bit_14_co, somador_1bit_15_co,
       somador_1bit_16_co, somador_1bit_17_co, somador_1bit_18_co, somador_1bit_19_co, somador_1bit_20_co,
       somador_1bit_21_co, somador_1bit_22_co, somador_1bit_23_co, somador_1bit_24_co, somador_1bit_25_co,
       somador_1bit_26_co, somador_1bit_27_co, somador_1bit_28_co, somador_1bit_29_co, somador_1bit_30_co,
       somador_1bit_31_co;

  Somador_1bit somador_1bit_1 (.Ci(Ci), .A(A[0]), .B(B[0]), .S(S[0]), .Co(somador_1bit_1_co));
  Somador_1bit somador_1bit_2 (.Ci(somador_1bit_1_co), .A(A[1]), .B(B[1]), .S(S[1]), .Co(somador_1bit_2_co));
  Somador_1bit somador_1bit_3 (.Ci(somador_1bit_2_co), .A(A[2]), .B(B[2]), .S(S[2]), .Co(somador_1bit_3_co));
  Somador_1bit somador_1bit_4 (.Ci(somador_1bit_3_co), .A(A[3]), .B(B[3]), .S(S[3]), .Co(somador_1bit_4_co));
  Somador_1bit somador_1bit_5 (.Ci(somador_1bit_4_co), .A(A[4]), .B(B[4]), .S(S[4]), .Co(somador_1bit_5_co));
  Somador_1bit somador_1bit_6 (.Ci(somador_1bit_5_co), .A(A[5]), .B(B[5]), .S(S[5]), .Co(somador_1bit_6_co));
  Somador_1bit somador_1bit_7 (.Ci(somador_1bit_6_co), .A(A[6]), .B(B[6]), .S(S[6]), .Co(somador_1bit_7_co));
  Somador_1bit somador_1bit_8 (.Ci(somador_1bit_7_co), .A(A[7]), .B(B[7]), .S(S[7]), .Co(somador_1bit_8_co));
  Somador_1bit somador_1bit_9 (.Ci(somador_1bit_8_co), .A(A[8]), .B(B[8]), .S(S[8]), .Co(somador_1bit_9_co));
  Somador_1bit somador_1bit_10 (.Ci(somador_1bit_9_co), .A(A[9]), .B(B[9]), .S(S[9]), .Co(somador_1bit_10_co));
  Somador_1bit somador_1bit_11 (.Ci(somador_1bit_10_co), .A(A[10]), .B(B[10]), .S(S[10]), .Co(somador_1bit_11_co));
  Somador_1bit somador_1bit_12 (.Ci(somador_1bit_11_co), .A(A[11]), .B(B[11]), .S(S[11]), .Co(somador_1bit_12_co));
  Somador_1bit somador_1bit_13 (.Ci(somador_1bit_12_co), .A(A[12]), .B(B[12]), .S(S[12]), .Co(somador_1bit_13_co));
  Somador_1bit somador_1bit_14 (.Ci(somador_1bit_13_co), .A(A[13]), .B(B[13]), .S(S[13]), .Co(somador_1bit_14_co));
  Somador_1bit somador_1bit_15 (.Ci(somador_1bit_14_co), .A(A[14]), .B(B[14]), .S(S[14]), .Co(somador_1bit_15_co));
  Somador_1bit somador_1bit_16 (.Ci(somador_1bit_15_co), .A(A[15]), .B(B[15]), .S(S[15]), .Co(somador_1bit_16_co));
  Somador_1bit somador_1bit_17 (.Ci(somador_1bit_16_co), .A(A[16]), .B(B[16]), .S(S[16]), .Co(somador_1bit_17_co));
  Somador_1bit somador_1bit_18 (.Ci(somador_1bit_17_co), .A(A[17]), .B(B[17]), .S(S[17]), .Co(somador_1bit_18_co));
  Somador_1bit somador_1bit_19 (.Ci(somador_1bit_18_co), .A(A[18]), .B(B[18]), .S(S[18]), .Co(somador_1bit_19_co));
  Somador_1bit somador_1bit_20 (.Ci(somador_1bit_19_co), .A(A[19]), .B(B[19]), .S(S[19]), .Co(somador_1bit_20_co));
  Somador_1bit somador_1bit_21 (.Ci(somador_1bit_20_co), .A(A[20]), .B(B[20]), .S(S[20]), .Co(somador_1bit_21_co));
  Somador_1bit somador_1bit_22 (.Ci(somador_1bit_21_co), .A(A[21]), .B(B[21]), .S(S[21]), .Co(somador_1bit_22_co));
  Somador_1bit somador_1bit_23 (.Ci(somador_1bit_22_co), .A(A[22]), .B(B[22]), .S(S[22]), .Co(somador_1bit_23_co));
  Somador_1bit somador_1bit_24 (.Ci(somador_1bit_23_co), .A(A[23]), .B(B[23]), .S(S[23]), .Co(somador_1bit_24_co));
  Somador_1bit somador_1bit_25 (.Ci(somador_1bit_24_co), .A(A[24]), .B(B[24]), .S(S[24]), .Co(somador_1bit_25_co));
  Somador_1bit somador_1bit_26 (.Ci(somador_1bit_25_co), .A(A[25]), .B(B[25]), .S(S[25]), .Co(somador_1bit_26_co));
  Somador_1bit somador_1bit_27 (.Ci(somador_1bit_26_co), .A(A[26]), .B(B[26]), .S(S[26]), .Co(somador_1bit_27_co));
  Somador_1bit somador_1bit_28 (.Ci(somador_1bit_27_co), .A(A[27]), .B(B[27]), .S(S[27]), .Co(somador_1bit_28_co));
  Somador_1bit somador_1bit_29 (.Ci(somador_1bit_28_co), .A(A[28]), .B(B[28]), .S(S[28]), .Co(somador_1bit_29_co));
  Somador_1bit somador_1bit_30 (.Ci(somador_1bit_29_co), .A(A[29]), .B(B[29]), .S(S[29]), .Co(somador_1bit_30_co));
  Somador_1bit somador_1bit_31 (.Ci(somador_1bit_30_co), .A(A[30]), .B(B[30]), .S(S[30]), .Co(somador_1bit_31_co));
  Somador_1bit somador_1bit_32 (.Ci(somador_1bit_31_co), .A(A[31]), .B(B[31]), .S(S[31]));  // open: Co
endmodule

module Deslocador_32bits (
  input  [31:0] A,
  input  [31:0] B,
  output [31:0] S
);

  Multiplexer #(.select(5)) multiplexer_1 (
    .in0(A[31]), .in1(A[30]), .in2(A[29]), .in3(A[28]), .in4(A[27]), .in5(A[26]), .in6(A[25]), .in7(A[24]),
    .in8(A[23]), .in9(A[22]), .in10(A[21]), .in11(A[20]), .in12(A[19]), .in13(A[18]), .in14(A[17]),
    .in15(A[16]), .in16(A[15]), .in17(A[14]), .in18(A[13]), .in19(A[12]), .in20(A[11]), .in21(A[10]),
    .in22(A[9]), .in23(A[8]), .in24(A[7]), .in25(A[6]), .in26(A[5]), .in27(A[4]), .in28(A[3]), .in29(A[2]),
    .in30(A[1]), .in31(A[0]), .out(S[31]), .sel(B[4:0]));
  Multiplexer #(.select(5)) multiplexer_2 (
    .in0(A[30]), .in1(A[29]), .in2(A[28]), .in3(A[27]), .in4(A[26]), .in5(A[25]), .in6(A[24]), .in7(A[23]),
    .in8(A[22]), .in9(A[21]), .in10(A[20]), .in11(A[19]), .in12(A[18]), .in13(A[17]), .in14(A[16]),
    .in15(A[15]), .in16(A[14]), .in17(A[13]), .in18(A[12]), .in19(A[11]), .in20(A[10]), .in21(A[9]),
    .in22(A[8]), .in23(A[7]), .in24(A[6]), .in25(A[5]), .in26(A[4]), .in27(A[3]), .in28(A[2]), .in29(A[1]),
    .in30(A[0]), .in31(1'b0), .out(S[30]), .sel(B[4:0]));
  Multiplexer #(.select(5)) multiplexer_3 (
    .in0(A[29]), .in1(A[28]), .in2(A[27]), .in3(A[26]), .in4(A[25]), .in5(A[24]), .in6(A[23]), .in7(A[22]),
    .in8(A[21]), .in9(A[20]), .in10(A[19]), .in11(A[18]), .in12(A[17]), .in13(A[16]), .in14(A[15]),
    .in15(A[14]), .in16(A[13]), .in17(A[12]), .in18(A[11]), .in19(A[10]), .in20(A[9]), .in21(A[8]),
    .in22(A[7]), .in23(A[6]), .in24(A[5]), .in25(A[4]), .in26(A[3]), .in27(A[2]), .in28(A[1]), .in29(A[0]),
    .in30(1'b0), .in31(1'b0), .out(S[29]), .sel(B[4:0]));
  Multiplexer #(.select(5)) multiplexer_4 (
    .in0(A[28]), .in1(A[27]), .in2(A[26]), .in3(A[25]), .in4(A[24]), .in5(A[23]), .in6(A[22]), .in7(A[21]),
    .in8(A[20]), .in9(A[19]), .in10(A[18]), .in11(A[17]), .in12(A[16]), .in13(A[15]), .in14(A[14]),
    .in15(A[13]), .in16(A[12]), .in17(A[11]), .in18(A[10]), .in19(A[9]), .in20(A[8]), .in21(A[7]),
    .in22(A[6]), .in23(A[5]), .in24(A[4]), .in25(A[3]), .in26(A[2]), .in27(A[1]), .in28(A[0]), .in29(1'b0),
    .in30(1'b0), .in31(1'b0), .out(S[28]), .sel(B[4:0]));
  Multiplexer #(.select(5)) multiplexer_5 (
    .in0(A[27]), .in1(A[26]), .in2(A[25]), .in3(A[24]), .in4(A[23]), .in5(A[22]), .in6(A[21]), .in7(A[20]),
    .in8(A[19]), .in9(A[18]), .in10(A[17]), .in11(A[16]), .in12(A[15]), .in13(A[14]), .in14(A[13]),
    .in15(A[12]), .in16(A[11]), .in17(A[10]), .in18(A[9]), .in19(A[8]), .in20(A[7]), .in21(A[6]),
    .in22(A[5]), .in23(A[4]), .in24(A[3]), .in25(A[2]), .in26(A[1]), .in27(A[0]), .in28(1'b0), .in29(1'b0),
    .in30(1'b0), .in31(1'b0), .out(S[27]), .sel(B[4:0]));
  Multiplexer #(.select(5)) multiplexer_6 (
    .in0(A[26]), .in1(A[25]), .in2(A[24]), .in3(A[23]), .in4(A[22]), .in5(A[21]), .in6(A[20]), .in7(A[19]),
    .in8(A[18]), .in9(A[17]), .in10(A[16]), .in11(A[15]), .in12(A[14]), .in13(A[13]), .in14(A[12]),
    .in15(A[11]), .in16(A[10]), .in17(A[9]), .in18(A[8]), .in19(A[7]), .in20(A[6]), .in21(A[5]), .in22(A[4]),
    .in23(A[3]), .in24(A[2]), .in25(A[1]), .in26(A[0]), .in27(1'b0), .in28(1'b0), .in29(1'b0), .in30(1'b0),
    .in31(1'b0), .out(S[26]), .sel(B[4:0]));
  Multiplexer #(.select(5)) multiplexer_7 (
    .in0(A[25]), .in1(A[24]), .in2(A[23]), .in3(A[22]), .in4(A[21]), .in5(A[20]), .in6(A[19]), .in7(A[18]),
    .in8(A[17]), .in9(A[16]), .in10(A[15]), .in11(A[14]), .in12(A[13]), .in13(A[12]), .in14(A[11]),
    .in15(A[10]), .in16(A[9]), .in17(A[8]), .in18(A[7]), .in19(A[6]), .in20(A[5]), .in21(A[4]), .in22(A[3]),
    .in23(A[2]), .in24(A[1]), .in25(A[0]), .in26(1'b0), .in27(1'b0), .in28(1'b0), .in29(1'b0), .in30(1'b0),
    .in31(1'b0), .out(S[25]), .sel(B[4:0]));
  Multiplexer #(.select(5)) multiplexer_8 (
    .in0(A[24]), .in1(A[23]), .in2(A[22]), .in3(A[21]), .in4(A[20]), .in5(A[19]), .in6(A[18]), .in7(A[17]),
    .in8(A[16]), .in9(A[15]), .in10(A[14]), .in11(A[13]), .in12(A[12]), .in13(A[11]), .in14(A[10]),
    .in15(A[9]), .in16(A[8]), .in17(A[7]), .in18(A[6]), .in19(A[5]), .in20(A[4]), .in21(A[3]), .in22(A[2]),
    .in23(A[1]), .in24(A[0]), .in25(1'b0), .in26(1'b0), .in27(1'b0), .in28(1'b0), .in29(1'b0), .in30(1'b0),
    .in31(1'b0), .out(S[24]), .sel(B[4:0]));
  Multiplexer #(.select(5)) multiplexer_9 (
    .in0(A[23]), .in1(A[22]), .in2(A[21]), .in3(A[20]), .in4(A[19]), .in5(A[18]), .in6(A[17]), .in7(A[16]),
    .in8(A[15]), .in9(A[14]), .in10(A[13]), .in11(A[12]), .in12(A[11]), .in13(A[10]), .in14(A[9]),
    .in15(A[8]), .in16(A[7]), .in17(A[6]), .in18(A[5]), .in19(A[4]), .in20(A[3]), .in21(A[2]), .in22(A[1]),
    .in23(A[0]), .in24(1'b0), .in25(1'b0), .in26(1'b0), .in27(1'b0), .in28(1'b0), .in29(1'b0), .in30(1'b0),
    .in31(1'b0), .out(S[23]), .sel(B[4:0]));
  Multiplexer #(.select(5)) multiplexer_10 (
    .in0(A[22]), .in1(A[21]), .in2(A[20]), .in3(A[19]), .in4(A[18]), .in5(A[17]), .in6(A[16]), .in7(A[15]),
    .in8(A[14]), .in9(A[13]), .in10(A[12]), .in11(A[11]), .in12(A[10]), .in13(A[9]), .in14(A[8]),
    .in15(A[7]), .in16(A[6]), .in17(A[5]), .in18(A[4]), .in19(A[3]), .in20(A[2]), .in21(A[1]), .in22(A[0]),
    .in23(1'b0), .in24(1'b0), .in25(1'b0), .in26(1'b0), .in27(1'b0), .in28(1'b0), .in29(1'b0), .in30(1'b0),
    .in31(1'b0), .out(S[22]), .sel(B[4:0]));
  Multiplexer #(.select(5)) multiplexer_11 (
    .in0(A[21]), .in1(A[20]), .in2(A[19]), .in3(A[18]), .in4(A[17]), .in5(A[16]), .in6(A[15]), .in7(A[14]),
    .in8(A[13]), .in9(A[12]), .in10(A[11]), .in11(A[10]), .in12(A[9]), .in13(A[8]), .in14(A[7]), .in15(A[6]),
    .in16(A[5]), .in17(A[4]), .in18(A[3]), .in19(A[2]), .in20(A[1]), .in21(A[0]), .in22(1'b0), .in23(1'b0),
    .in24(1'b0), .in25(1'b0), .in26(1'b0), .in27(1'b0), .in28(1'b0), .in29(1'b0), .in30(1'b0), .in31(1'b0),
    .out(S[21]), .sel(B[4:0]));
  Multiplexer #(.select(5)) multiplexer_12 (
    .in0(A[20]), .in1(A[19]), .in2(A[18]), .in3(A[17]), .in4(A[16]), .in5(A[15]), .in6(A[14]), .in7(A[13]),
    .in8(A[12]), .in9(A[11]), .in10(A[10]), .in11(A[9]), .in12(A[8]), .in13(A[7]), .in14(A[6]), .in15(A[5]),
    .in16(A[4]), .in17(A[3]), .in18(A[2]), .in19(A[1]), .in20(A[0]), .in21(1'b0), .in22(1'b0), .in23(1'b0),
    .in24(1'b0), .in25(1'b0), .in26(1'b0), .in27(1'b0), .in28(1'b0), .in29(1'b0), .in30(1'b0), .in31(1'b0),
    .out(S[20]), .sel(B[4:0]));
  Multiplexer #(.select(5)) multiplexer_13 (
    .in0(A[19]), .in1(A[18]), .in2(A[17]), .in3(A[16]), .in4(A[15]), .in5(A[14]), .in6(A[13]), .in7(A[12]),
    .in8(A[11]), .in9(A[10]), .in10(A[9]), .in11(A[8]), .in12(A[7]), .in13(A[6]), .in14(A[5]), .in15(A[4]),
    .in16(A[3]), .in17(A[2]), .in18(A[1]), .in19(A[0]), .in20(1'b0), .in21(1'b0), .in22(1'b0), .in23(1'b0),
    .in24(1'b0), .in25(1'b0), .in26(1'b0), .in27(1'b0), .in28(1'b0), .in29(1'b0), .in30(1'b0), .in31(1'b0),
    .out(S[19]), .sel(B[4:0]));
  Multiplexer #(.select(5)) multiplexer_14 (
    .in0(A[18]), .in1(A[17]), .in2(A[16]), .in3(A[15]), .in4(A[14]), .in5(A[13]), .in6(A[12]), .in7(A[11]),
    .in8(A[10]), .in9(A[9]), .in10(A[8]), .in11(A[7]), .in12(A[6]), .in13(A[5]), .in14(A[4]), .in15(A[3]),
    .in16(A[2]), .in17(A[1]), .in18(A[0]), .in19(1'b0), .in20(1'b0), .in21(1'b0), .in22(1'b0), .in23(1'b0),
    .in24(1'b0), .in25(1'b0), .in26(1'b0), .in27(1'b0), .in28(1'b0), .in29(1'b0), .in30(1'b0), .in31(1'b0),
    .out(S[18]), .sel(B[4:0]));
  Multiplexer #(.select(5)) multiplexer_15 (
    .in0(A[17]), .in1(A[16]), .in2(A[15]), .in3(A[14]), .in4(A[13]), .in5(A[12]), .in6(A[11]), .in7(A[10]),
    .in8(A[9]), .in9(A[8]), .in10(A[7]), .in11(A[6]), .in12(A[5]), .in13(A[4]), .in14(A[3]), .in15(A[2]),
    .in16(A[1]), .in17(A[0]), .in18(1'b0), .in19(1'b0), .in20(1'b0), .in21(1'b0), .in22(1'b0), .in23(1'b0),
    .in24(1'b0), .in25(1'b0), .in26(1'b0), .in27(1'b0), .in28(1'b0), .in29(1'b0), .in30(1'b0), .in31(1'b0),
    .out(S[17]), .sel(B[4:0]));
  Multiplexer #(.select(5)) multiplexer_16 (
    .in0(A[16]), .in1(A[15]), .in2(A[14]), .in3(A[13]), .in4(A[12]), .in5(A[11]), .in6(A[10]), .in7(A[9]),
    .in8(A[8]), .in9(A[7]), .in10(A[6]), .in11(A[5]), .in12(A[4]), .in13(A[3]), .in14(A[2]), .in15(A[1]),
    .in16(A[0]), .in17(1'b0), .in18(1'b0), .in19(1'b0), .in20(1'b0), .in21(1'b0), .in22(1'b0), .in23(1'b0),
    .in24(1'b0), .in25(1'b0), .in26(1'b0), .in27(1'b0), .in28(1'b0), .in29(1'b0), .in30(1'b0), .in31(1'b0),
    .out(S[16]), .sel(B[4:0]));
  Multiplexer #(.select(5)) multiplexer_17 (
    .in0(A[15]), .in1(A[14]), .in2(A[13]), .in3(A[12]), .in4(A[11]), .in5(A[10]), .in6(A[9]), .in7(A[8]),
    .in8(A[7]), .in9(A[6]), .in10(A[5]), .in11(A[4]), .in12(A[3]), .in13(A[2]), .in14(A[1]), .in15(A[0]),
    .in16(1'b0), .in17(1'b0), .in18(1'b0), .in19(1'b0), .in20(1'b0), .in21(1'b0), .in22(1'b0), .in23(1'b0),
    .in24(1'b0), .in25(1'b0), .in26(1'b0), .in27(1'b0), .in28(1'b0), .in29(1'b0), .in30(1'b0), .in31(1'b0),
    .out(S[15]), .sel(B[4:0]));
  Multiplexer #(.select(5)) multiplexer_18 (
    .in0(A[14]), .in1(A[13]), .in2(A[12]), .in3(A[11]), .in4(A[10]), .in5(A[9]), .in6(A[8]), .in7(A[7]),
    .in8(A[6]), .in9(A[5]), .in10(A[4]), .in11(A[3]), .in12(A[2]), .in13(A[1]), .in14(A[0]), .in15(1'b0),
    .in16(1'b0), .in17(1'b0), .in18(1'b0), .in19(1'b0), .in20(1'b0), .in21(1'b0), .in22(1'b0), .in23(1'b0),
    .in24(1'b0), .in25(1'b0), .in26(1'b0), .in27(1'b0), .in28(1'b0), .in29(1'b0), .in30(1'b0), .in31(1'b0),
    .out(S[14]), .sel(B[4:0]));
  Multiplexer #(.select(5)) multiplexer_19 (
    .in0(A[13]), .in1(A[12]), .in2(A[11]), .in3(A[10]), .in4(A[9]), .in5(A[8]), .in6(A[7]), .in7(A[6]),
    .in8(A[5]), .in9(A[4]), .in10(A[3]), .in11(A[2]), .in12(A[1]), .in13(A[0]), .in14(1'b0), .in15(1'b0),
    .in16(1'b0), .in17(1'b0), .in18(1'b0), .in19(1'b0), .in20(1'b0), .in21(1'b0), .in22(1'b0), .in23(1'b0),
    .in24(1'b0), .in25(1'b0), .in26(1'b0), .in27(1'b0), .in28(1'b0), .in29(1'b0), .in30(1'b0), .in31(1'b0),
    .out(S[13]), .sel(B[4:0]));
  Multiplexer #(.select(5)) multiplexer_20 (
    .in0(A[12]), .in1(A[11]), .in2(A[10]), .in3(A[9]), .in4(A[8]), .in5(A[7]), .in6(A[6]), .in7(A[5]),
    .in8(A[4]), .in9(A[3]), .in10(A[2]), .in11(A[1]), .in12(A[0]), .in13(1'b0), .in14(1'b0), .in15(1'b0),
    .in16(1'b0), .in17(1'b0), .in18(1'b0), .in19(1'b0), .in20(1'b0), .in21(1'b0), .in22(1'b0), .in23(1'b0),
    .in24(1'b0), .in25(1'b0), .in26(1'b0), .in27(1'b0), .in28(1'b0), .in29(1'b0), .in30(1'b0), .in31(1'b0),
    .out(S[12]), .sel(B[4:0]));
  Multiplexer #(.select(5)) multiplexer_21 (
    .in0(A[11]), .in1(A[10]), .in2(A[9]), .in3(A[8]), .in4(A[7]), .in5(A[6]), .in6(A[5]), .in7(A[4]),
    .in8(A[3]), .in9(A[2]), .in10(A[1]), .in11(A[0]), .in12(1'b0), .in13(1'b0), .in14(1'b0), .in15(1'b0),
    .in16(1'b0), .in17(1'b0), .in18(1'b0), .in19(1'b0), .in20(1'b0), .in21(1'b0), .in22(1'b0), .in23(1'b0),
    .in24(1'b0), .in25(1'b0), .in26(1'b0), .in27(1'b0), .in28(1'b0), .in29(1'b0), .in30(1'b0), .in31(1'b0),
    .out(S[11]), .sel(B[4:0]));
  Multiplexer #(.select(5)) multiplexer_22 (
    .in0(A[10]), .in1(A[9]), .in2(A[8]), .in3(A[7]), .in4(A[6]), .in5(A[5]), .in6(A[4]), .in7(A[3]),
    .in8(A[2]), .in9(A[1]), .in10(A[0]), .in11(1'b0), .in12(1'b0), .in13(1'b0), .in14(1'b0), .in15(1'b0),
    .in16(1'b0), .in17(1'b0), .in18(1'b0), .in19(1'b0), .in20(1'b0), .in21(1'b0), .in22(1'b0), .in23(1'b0),
    .in24(1'b0), .in25(1'b0), .in26(1'b0), .in27(1'b0), .in28(1'b0), .in29(1'b0), .in30(1'b0), .in31(1'b0),
    .out(S[10]), .sel(B[4:0]));
  Multiplexer #(.select(5)) multiplexer_23 (
    .in0(A[9]), .in1(A[8]), .in2(A[7]), .in3(A[6]), .in4(A[5]), .in5(A[4]), .in6(A[3]), .in7(A[2]),
    .in8(A[1]), .in9(A[0]), .in10(1'b0), .in11(1'b0), .in12(1'b0), .in13(1'b0), .in14(1'b0), .in15(1'b0),
    .in16(1'b0), .in17(1'b0), .in18(1'b0), .in19(1'b0), .in20(1'b0), .in21(1'b0), .in22(1'b0), .in23(1'b0),
    .in24(1'b0), .in25(1'b0), .in26(1'b0), .in27(1'b0), .in28(1'b0), .in29(1'b0), .in30(1'b0), .in31(1'b0),
    .out(S[9]), .sel(B[4:0]));
  Multiplexer #(.select(5)) multiplexer_24 (
    .in0(A[8]), .in1(A[7]), .in2(A[6]), .in3(A[5]), .in4(A[4]), .in5(A[3]), .in6(A[2]), .in7(A[1]),
    .in8(A[0]), .in9(1'b0), .in10(1'b0), .in11(1'b0), .in12(1'b0), .in13(1'b0), .in14(1'b0), .in15(1'b0),
    .in16(1'b0), .in17(1'b0), .in18(1'b0), .in19(1'b0), .in20(1'b0), .in21(1'b0), .in22(1'b0), .in23(1'b0),
    .in24(1'b0), .in25(1'b0), .in26(1'b0), .in27(1'b0), .in28(1'b0), .in29(1'b0), .in30(1'b0), .in31(1'b0),
    .out(S[8]), .sel(B[4:0]));
  Multiplexer #(.select(5)) multiplexer_25 (
    .in0(A[7]), .in1(A[6]), .in2(A[5]), .in3(A[4]), .in4(A[3]), .in5(A[2]), .in6(A[1]), .in7(A[0]),
    .in8(1'b0), .in9(1'b0), .in10(1'b0), .in11(1'b0), .in12(1'b0), .in13(1'b0), .in14(1'b0), .in15(1'b0),
    .in16(1'b0), .in17(1'b0), .in18(1'b0), .in19(1'b0), .in20(1'b0), .in21(1'b0), .in22(1'b0), .in23(1'b0),
    .in24(1'b0), .in25(1'b0), .in26(1'b0), .in27(1'b0), .in28(1'b0), .in29(1'b0), .in30(1'b0), .in31(1'b0),
    .out(S[7]), .sel(B[4:0]));
  Multiplexer #(.select(5)) multiplexer_26 (
    .in0(A[6]), .in1(A[5]), .in2(A[4]), .in3(A[3]), .in4(A[2]), .in5(A[1]), .in6(A[0]), .in7(1'b0),
    .in8(1'b0), .in9(1'b0), .in10(1'b0), .in11(1'b0), .in12(1'b0), .in13(1'b0), .in14(1'b0), .in15(1'b0),
    .in16(1'b0), .in17(1'b0), .in18(1'b0), .in19(1'b0), .in20(1'b0), .in21(1'b0), .in22(1'b0), .in23(1'b0),
    .in24(1'b0), .in25(1'b0), .in26(1'b0), .in27(1'b0), .in28(1'b0), .in29(1'b0), .in30(1'b0), .in31(1'b0),
    .out(S[6]), .sel(B[4:0]));
  Multiplexer #(.select(5)) multiplexer_27 (
    .in0(A[5]), .in1(A[4]), .in2(A[3]), .in3(A[2]), .in4(A[1]), .in5(A[0]), .in6(1'b0), .in7(1'b0),
    .in8(1'b0), .in9(1'b0), .in10(1'b0), .in11(1'b0), .in12(1'b0), .in13(1'b0), .in14(1'b0), .in15(1'b0),
    .in16(1'b0), .in17(1'b0), .in18(1'b0), .in19(1'b0), .in20(1'b0), .in21(1'b0), .in22(1'b0), .in23(1'b0),
    .in24(1'b0), .in25(1'b0), .in26(1'b0), .in27(1'b0), .in28(1'b0), .in29(1'b0), .in30(1'b0), .in31(1'b0),
    .out(S[5]), .sel(B[4:0]));
  Multiplexer #(.select(5)) multiplexer_28 (
    .in0(A[4]), .in1(A[3]), .in2(A[2]), .in3(A[1]), .in4(A[0]), .in5(1'b0), .in6(1'b0), .in7(1'b0),
    .in8(1'b0), .in9(1'b0), .in10(1'b0), .in11(1'b0), .in12(1'b0), .in13(1'b0), .in14(1'b0), .in15(1'b0),
    .in16(1'b0), .in17(1'b0), .in18(1'b0), .in19(1'b0), .in20(1'b0), .in21(1'b0), .in22(1'b0), .in23(1'b0),
    .in24(1'b0), .in25(1'b0), .in26(1'b0), .in27(1'b0), .in28(1'b0), .in29(1'b0), .in30(1'b0), .in31(1'b0),
    .out(S[4]), .sel(B[4:0]));
  Multiplexer #(.select(5)) multiplexer_29 (
    .in0(A[3]), .in1(A[2]), .in2(A[1]), .in3(A[0]), .in4(1'b0), .in5(1'b0), .in6(1'b0), .in7(1'b0),
    .in8(1'b0), .in9(1'b0), .in10(1'b0), .in11(1'b0), .in12(1'b0), .in13(1'b0), .in14(1'b0), .in15(1'b0),
    .in16(1'b0), .in17(1'b0), .in18(1'b0), .in19(1'b0), .in20(1'b0), .in21(1'b0), .in22(1'b0), .in23(1'b0),
    .in24(1'b0), .in25(1'b0), .in26(1'b0), .in27(1'b0), .in28(1'b0), .in29(1'b0), .in30(1'b0), .in31(1'b0),
    .out(S[3]), .sel(B[4:0]));
  Multiplexer #(.select(5)) multiplexer_30 (
    .in0(A[2]), .in1(A[1]), .in2(A[0]), .in3(1'b0), .in4(1'b0), .in5(1'b0), .in6(1'b0), .in7(1'b0),
    .in8(1'b0), .in9(1'b0), .in10(1'b0), .in11(1'b0), .in12(1'b0), .in13(1'b0), .in14(1'b0), .in15(1'b0),
    .in16(1'b0), .in17(1'b0), .in18(1'b0), .in19(1'b0), .in20(1'b0), .in21(1'b0), .in22(1'b0), .in23(1'b0),
    .in24(1'b0), .in25(1'b0), .in26(1'b0), .in27(1'b0), .in28(1'b0), .in29(1'b0), .in30(1'b0), .in31(1'b0),
    .out(S[2]), .sel(B[4:0]));
  Multiplexer #(.select(5)) multiplexer_31 (
    .in0(A[1]), .in1(A[0]), .in2(1'b0), .in3(1'b0), .in4(1'b0), .in5(1'b0), .in6(1'b0), .in7(1'b0),
    .in8(1'b0), .in9(1'b0), .in10(1'b0), .in11(1'b0), .in12(1'b0), .in13(1'b0), .in14(1'b0), .in15(1'b0),
    .in16(1'b0), .in17(1'b0), .in18(1'b0), .in19(1'b0), .in20(1'b0), .in21(1'b0), .in22(1'b0), .in23(1'b0),
    .in24(1'b0), .in25(1'b0), .in26(1'b0), .in27(1'b0), .in28(1'b0), .in29(1'b0), .in30(1'b0), .in31(1'b0),
    .out(S[1]), .sel(B[4:0]));
  Multiplexer #(.select(5)) multiplexer_32 (
    .in0(A[0]), .in1(1'b0), .in2(1'b0), .in3(1'b0), .in4(1'b0), .in5(1'b0), .in6(1'b0), .in7(1'b0),
    .in8(1'b0), .in9(1'b0), .in10(1'b0), .in11(1'b0), .in12(1'b0), .in13(1'b0), .in14(1'b0), .in15(1'b0),
    .in16(1'b0), .in17(1'b0), .in18(1'b0), .in19(1'b0), .in20(1'b0), .in21(1'b0), .in22(1'b0), .in23(1'b0),
    .in24(1'b0), .in25(1'b0), .in26(1'b0), .in27(1'b0), .in28(1'b0), .in29(1'b0), .in30(1'b0), .in31(1'b0),
    .out(S[0]), .sel(B[4:0]));

  // Other names for the same wires on the sheet: B_t[4:0] = B[4:0]
endmodule

module Somador_1bit (
  input  Ci,
  input  A,
  input  B,
  output S,
  output Co
);

  wire and_1_out, and_2_out, or_1_out, xor_1_out;

  xor xor_1 (xor_1_out, Ci, A);
  or or_1 (or_1_out, A, B);
  xor xor_2 (S, xor_1_out, B);
  and and_1 (and_1_out, A, B);
  and and_2 (and_2_out, or_1_out, Ci);
  or or_2 (Co, and_1_out, and_2_out);
endmodule

module ULA (
  input  [2:0] Funct,
  input  [31:0] A,
  input  [31:0] B,
  output Zero,
  output [31:0] S
);

  wire and_1_out, and_2_out, and_3_out, and_4_out, and_5_out, and_6_out, and_7_out, and_8_out, and_9_out,
       and_10_out;
  wire [31:0] and_32bits_1_y, deslocador_32bits_1_s, multiplicador_32bits_1_y, not_1_out, not_2_out,
       or_32bits_1_y, somador_32bits_1_s, somador_32bits_2_s, xor_32bits_1_y;

  // Probe on A
  // Probe on B
  assign not_1_out = ~B;  // NOT_Gate not_1, 32 bits wide
  Somador_32bits somador_32bits_1 (.Ci(1'b0), .A(A), .B(B), .S(somador_32bits_1_s));
  Somador_32bits somador_32bits_2 (.Ci(1'b1), .A(A), .B(not_1_out), .S(somador_32bits_2_s));
  Multiplicador_32bits multiplicador_32bits_1 (.A(A), .B(B), .Y(multiplicador_32bits_1_y));
  AND_32bits and_32bits_1 (.A(A), .B(B), .Y(and_32bits_1_y));
  OR_32bits or_32bits_1 (.A(A), .B(B), .Y(or_32bits_1_y));
  XOR_32bits xor_32bits_1 (.A(A), .B(B), .Y(xor_32bits_1_y));
  Deslocador_32bits deslocador_32bits_1 (.A(A), .B(B), .S(deslocador_32bits_1_s));
  Multiplexer #(.select(3), .width(32)) multiplexer_1 (
    .in0(somador_32bits_1_s), .in1(somador_32bits_2_s), .in2(multiplicador_32bits_1_y), .in3(and_32bits_1_y),
    .in4(or_32bits_1_y), .in5(xor_32bits_1_y), .in6(deslocador_32bits_1_s), .out(S), .sel(Funct));  // open: in7
  assign not_2_out = ~S;  // NOT_Gate not_2, 32 bits wide
  // Probe on S
  and and_1 (and_1_out, not_2_out[31], not_2_out[30], not_2_out[29], not_2_out[28]);
  and and_2 (and_2_out, not_2_out[27], not_2_out[26], not_2_out[25], not_2_out[24]);
  and and_3 (and_3_out, not_2_out[23], not_2_out[22], not_2_out[21], not_2_out[20]);
  and and_4 (and_4_out, not_2_out[19], not_2_out[18], not_2_out[17], not_2_out[16]);
  and and_5 (and_5_out, not_2_out[15], not_2_out[14], not_2_out[13], not_2_out[12]);
  and and_6 (and_6_out, not_2_out[11], not_2_out[10], not_2_out[9], not_2_out[8]);
  and and_7 (and_7_out, not_2_out[7], not_2_out[6], not_2_out[5], not_2_out[4]);
  and and_8 (and_8_out, not_2_out[3], not_2_out[2], not_2_out[1], not_2_out[0]);
  and and_9 (and_9_out, and_1_out, and_2_out, and_3_out, and_4_out);
  and and_10 (and_10_out, and_5_out, and_6_out, and_7_out, and_8_out);
  and and_11 (Zero, and_9_out, and_10_out);
endmodule

module Subtrator_1bit (
  input  Ci,
  input  A,
  input  B,
  output S,
  output Co
);

  wire and_1_out, and_2_out, and_3_out, not_1_out, not_2_out, xor_1_out;

  not not_1 (not_1_out, Ci);
  not not_2 (not_2_out, A);
  xor xor_1 (xor_1_out, A, B);
  and and_1 (and_1_out, not_1_out, B);
  and and_2 (and_2_out, not_2_out, Ci);
  and and_3 (and_3_out, B, Ci);
  or or_1 (Co, and_1_out, and_2_out, and_3_out);
  xor xor_2 (S, xor_1_out, Ci);
endmodule

module Subtrator_32bits (
  input  Ci,
  input  [31:0] A,
  input  [31:0] B,
  output [31:0] S
);

  wire subtrator_1bit_1_co, subtrator_1bit_2_co, subtrator_1bit_3_co, subtrator_1bit_4_co,
       subtrator_1bit_5_co, subtrator_1bit_6_co, subtrator_1bit_7_co, subtrator_1bit_8_co,
       subtrator_1bit_9_co, subtrator_1bit_10_co, subtrator_1bit_11_co, subtrator_1bit_12_co,
       subtrator_1bit_13_co, subtrator_1bit_14_co, subtrator_1bit_15_co, subtrator_1bit_16_co,
       subtrator_1bit_17_co, subtrator_1bit_18_co, subtrator_1bit_19_co, subtrator_1bit_20_co,
       subtrator_1bit_21_co, subtrator_1bit_22_co, subtrator_1bit_23_co, subtrator_1bit_24_co,
       subtrator_1bit_25_co, subtrator_1bit_26_co, subtrator_1bit_27_co, subtrator_1bit_28_co,
       subtrator_1bit_29_co, subtrator_1bit_30_co, subtrator_1bit_31_co;

  Subtrator_1bit subtrator_1bit_1 (.Ci(Ci), .A(A[0]), .B(B[0]), .S(S[0]), .Co(subtrator_1bit_1_co));
  Subtrator_1bit subtrator_1bit_2 (.Ci(subtrator_1bit_1_co), .A(A[1]), .B(B[1]), .S(S[1]), .Co(subtrator_1bit_2_co));
  Subtrator_1bit subtrator_1bit_3 (.Ci(subtrator_1bit_2_co), .A(A[2]), .B(B[2]), .S(S[2]), .Co(subtrator_1bit_3_co));
  Subtrator_1bit subtrator_1bit_4 (.Ci(subtrator_1bit_3_co), .A(A[3]), .B(B[3]), .S(S[3]), .Co(subtrator_1bit_4_co));
  Subtrator_1bit subtrator_1bit_5 (.Ci(subtrator_1bit_4_co), .A(A[4]), .B(B[4]), .S(S[4]), .Co(subtrator_1bit_5_co));
  Subtrator_1bit subtrator_1bit_6 (.Ci(subtrator_1bit_5_co), .A(A[5]), .B(B[5]), .S(S[5]), .Co(subtrator_1bit_6_co));
  Subtrator_1bit subtrator_1bit_7 (.Ci(subtrator_1bit_6_co), .A(A[6]), .B(B[6]), .S(S[6]), .Co(subtrator_1bit_7_co));
  Subtrator_1bit subtrator_1bit_8 (.Ci(subtrator_1bit_7_co), .A(A[7]), .B(B[7]), .S(S[7]), .Co(subtrator_1bit_8_co));
  Subtrator_1bit subtrator_1bit_9 (.Ci(subtrator_1bit_8_co), .A(A[8]), .B(B[8]), .S(S[8]), .Co(subtrator_1bit_9_co));
  Subtrator_1bit subtrator_1bit_10 (.Ci(subtrator_1bit_9_co), .A(A[9]), .B(B[9]), .S(S[9]), .Co(subtrator_1bit_10_co));
  Subtrator_1bit subtrator_1bit_11 (
    .Ci(subtrator_1bit_10_co), .A(A[10]), .B(B[10]), .S(S[10]), .Co(subtrator_1bit_11_co));
  Subtrator_1bit subtrator_1bit_12 (
    .Ci(subtrator_1bit_11_co), .A(A[11]), .B(B[11]), .S(S[11]), .Co(subtrator_1bit_12_co));
  Subtrator_1bit subtrator_1bit_13 (
    .Ci(subtrator_1bit_12_co), .A(A[12]), .B(B[12]), .S(S[12]), .Co(subtrator_1bit_13_co));
  Subtrator_1bit subtrator_1bit_14 (
    .Ci(subtrator_1bit_13_co), .A(A[13]), .B(B[13]), .S(S[13]), .Co(subtrator_1bit_14_co));
  Subtrator_1bit subtrator_1bit_15 (
    .Ci(subtrator_1bit_14_co), .A(A[14]), .B(B[14]), .S(S[14]), .Co(subtrator_1bit_15_co));
  Subtrator_1bit subtrator_1bit_16 (
    .Ci(subtrator_1bit_15_co), .A(A[15]), .B(B[15]), .S(S[15]), .Co(subtrator_1bit_16_co));
  Subtrator_1bit subtrator_1bit_17 (
    .Ci(subtrator_1bit_16_co), .A(A[16]), .B(B[16]), .S(S[16]), .Co(subtrator_1bit_17_co));
  Subtrator_1bit subtrator_1bit_18 (
    .Ci(subtrator_1bit_17_co), .A(A[17]), .B(B[17]), .S(S[17]), .Co(subtrator_1bit_18_co));
  Subtrator_1bit subtrator_1bit_19 (
    .Ci(subtrator_1bit_18_co), .A(A[18]), .B(B[18]), .S(S[18]), .Co(subtrator_1bit_19_co));
  Subtrator_1bit subtrator_1bit_20 (
    .Ci(subtrator_1bit_19_co), .A(A[19]), .B(B[19]), .S(S[19]), .Co(subtrator_1bit_20_co));
  Subtrator_1bit subtrator_1bit_21 (
    .Ci(subtrator_1bit_20_co), .A(A[20]), .B(A[20]), .S(S[20]), .Co(subtrator_1bit_21_co));
  Subtrator_1bit subtrator_1bit_22 (
    .Ci(subtrator_1bit_21_co), .A(A[21]), .B(A[21]), .S(S[21]), .Co(subtrator_1bit_22_co));
  Subtrator_1bit subtrator_1bit_23 (
    .Ci(subtrator_1bit_22_co), .A(A[22]), .B(B[22]), .S(S[22]), .Co(subtrator_1bit_23_co));
  Subtrator_1bit subtrator_1bit_24 (
    .Ci(subtrator_1bit_23_co), .A(A[23]), .B(B[23]), .S(S[23]), .Co(subtrator_1bit_24_co));
  Subtrator_1bit subtrator_1bit_25 (
    .Ci(subtrator_1bit_24_co), .A(A[24]), .B(B[24]), .S(S[24]), .Co(subtrator_1bit_25_co));
  Subtrator_1bit subtrator_1bit_26 (
    .Ci(subtrator_1bit_25_co), .A(A[25]), .B(B[25]), .S(S[25]), .Co(subtrator_1bit_26_co));
  Subtrator_1bit subtrator_1bit_27 (
    .Ci(subtrator_1bit_26_co), .A(A[26]), .B(B[26]), .S(S[26]), .Co(subtrator_1bit_27_co));
  Subtrator_1bit subtrator_1bit_28 (
    .Ci(subtrator_1bit_27_co), .A(A[27]), .B(B[27]), .S(S[27]), .Co(subtrator_1bit_28_co));
  Subtrator_1bit subtrator_1bit_29 (
    .Ci(subtrator_1bit_28_co), .A(A[28]), .B(B[28]), .S(S[28]), .Co(subtrator_1bit_29_co));
  Subtrator_1bit subtrator_1bit_30 (
    .Ci(subtrator_1bit_29_co), .A(A[29]), .B(B[29]), .S(S[29]), .Co(subtrator_1bit_30_co));
  Subtrator_1bit subtrator_1bit_31 (
    .Ci(subtrator_1bit_30_co), .A(A[30]), .B(B[30]), .S(S[30]), .Co(subtrator_1bit_31_co));
  Subtrator_1bit subtrator_1bit_32 (.Ci(subtrator_1bit_31_co), .A(A[31]), .B(B[31]), .S(S[31]));  // open: Co
endmodule

module ExtensorZero (
  input  [15:0] A,
  output [31:0] B
);


  assign B = {{16{1'b0}}, A};
endmodule

module ExtensorSinal (
  input  [15:0] A,
  output [31:0] B
);


  assign B = {{17{A[15]}}, A[14:0]};
endmodule

module Registrador_4bits_PC (
  input  D0,
  input  D1,
  input  D2,
  input  D3,
  input  Clk,
  output Q0,
  output Q1,
  output Q2,
  output Q3
);

  wire d_ff_1_qn, d_ff_2_qn, d_ff_3_qn, d_ff_4_qn;

  D_Flip_Flop d_ff_1 (.D(D0), .clk(Clk), .Q(Q0), .Qn(d_ff_1_qn));  // open: preset, reset
  D_Flip_Flop d_ff_2 (.D(D1), .clk(Clk), .Q(Q1), .Qn(d_ff_2_qn));  // open: preset, reset
  D_Flip_Flop d_ff_3 (.D(D2), .clk(Clk), .Q(Q2), .Qn(d_ff_3_qn));  // open: preset, reset
  D_Flip_Flop d_ff_4 (.D(D3), .clk(Clk), .Q(Q3), .Qn(d_ff_4_qn));  // open: preset, reset
endmodule

module Registrador_32bits_PC (
  input  [31:0] D,
  input  Clk,
  output [31:0] Q
);

  Registrador_4bits_PC registrador_4bits_pc_1 (
    .D0(D[0]), .D1(D[1]), .D2(D[2]), .D3(D[3]), .Clk(Clk), .Q0(Q[0]), .Q1(Q[1]), .Q2(Q[2]), .Q3(Q[3]));
  Registrador_4bits_PC registrador_4bits_pc_2 (
    .D0(D[4]), .D1(D[5]), .D2(D[6]), .D3(D[7]), .Clk(Clk), .Q0(Q[4]), .Q1(Q[5]), .Q2(Q[6]), .Q3(Q[7]));
  Registrador_4bits_PC registrador_4bits_pc_3 (
    .D0(D[8]), .D1(D[9]), .D2(D[10]), .D3(D[11]), .Clk(Clk), .Q0(Q[8]), .Q1(Q[9]), .Q2(Q[10]), .Q3(Q[11]));
  Registrador_4bits_PC registrador_4bits_pc_4 (
    .D0(D[12]), .D1(D[13]), .D2(D[14]), .D3(D[15]), .Clk(Clk), .Q0(Q[12]), .Q1(Q[13]), .Q2(Q[14]), .Q3(Q[15]));
  Registrador_4bits_PC registrador_4bits_pc_5 (
    .D0(D[16]), .D1(D[17]), .D2(D[18]), .D3(D[19]), .Clk(Clk), .Q0(Q[16]), .Q1(Q[17]), .Q2(Q[18]), .Q3(Q[19]));
  Registrador_4bits_PC registrador_4bits_pc_6 (
    .D0(D[20]), .D1(D[21]), .D2(D[22]), .D3(D[23]), .Clk(Clk), .Q0(Q[20]), .Q1(Q[21]), .Q2(Q[22]), .Q3(Q[23]));
  Registrador_4bits_PC registrador_4bits_pc_7 (
    .D0(D[24]), .D1(D[25]), .D2(D[26]), .D3(D[27]), .Clk(Clk), .Q0(Q[24]), .Q1(Q[25]), .Q2(Q[26]), .Q3(Q[27]));
  Registrador_4bits_PC registrador_4bits_pc_8 (
    .D0(D[28]), .D1(D[29]), .D2(D[30]), .D3(D[31]), .Clk(Clk), .Q0(Q[28]), .Q1(Q[29]), .Q2(Q[30]), .Q3(Q[31]));
endmodule
